# Fritzing sketch schemaMontage (saved by Fritzing 0.9.3b)

parts:
  Composant1 = Arduino Uno (Rev3)
  BT1 = Bluetooth HC-06u [package=THT]
  Composant2 = NeoPixel Stick [part_number=1426]
  R1 = Resistor [tolerance=±5% resistance=10k package="0603 [SMD]"]
  R2 = Resistor [tolerance=±5% resistance=10k package="0603 [SMD]"]
  R3 = Resistor [tolerance=±5% resistance=10k package="0603 [SMD]"]
  S1 = Momentary Switch [package=ksa_sealed_tac_switch]
  R4 = Resistor [tolerance=±5% resistance=10k package="0603 [SMD]"]

nets:
  N1: Composant1.D10_PWM/SS, BT1.TXD
  N2: Composant1.D11_PWM/MOSI, R3.Pin_1
  N3: Composant1.D4, S1.4, R4.Pin_1
  N4: Composant1.D6_PWM, Composant2.+5V
  5V: Composant1.5V, BT1.VCC, Composant2.DATAIN, S1.1
  GND: Composant1.GND, BT1.GND, Composant2.GND, R2.Pin_1, R4.Pin_0
  N5: BT1.RXD, R1.Pin_0, R3.Pin_0

custom parts:
  Bluetooth HC-06u: Bluetooth HC-06 - face up, pins down 16.5mm x 37.5mm PCB
  NeoPixel Stick: Make your own little LED strip arrangement with this stick of NeoPixel LEDs. We crammed 8 of the tiny 5050 (5mm x 5mm) smart RGB LEDs onto a PCB with mounting holes and a chainable design. Use only one microcontroller pin to control as many as you can chain together! Each LED is addressable as the driver chip is inside the LED. Each one has ~18mA constant current drive so the color will be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
